# Fritzing sketch pcb (saved by Fritzing 0.9.10b)
breadboards: 1

parts:
  Raspberry_Pi_1 = Raspberry Pi 3 [part_number=RPI-3-V1.2]  # not connected
  LED1 = LED - 5mm [color="Yellow (585nm)" current=0.030 package="5 mm [THT]"]  # not connected
  S1 = Pushbutton [package="[SMD]"]
  LED2 = LED - 5mm [color="Blue (525nm)" current=0.030 package="5 mm [THT]"]

nets:
  N1: S1.Pin_1, S1.Pin_2, LED2.anode

notes:
  It might be advisable to add some resistors in the LED circuits to prevent them from burning out.
